// Logisim project ByteAlignment261C.circ as structural Verilog
module CPU16bits (
  input  BE,
  input  LW,
  input  LH,
  input  LHU,
  input  [19:0] Dir,
  output [15:0] Acumulador
);

  wire and_1_out, or_1_out;
  wire [15:0] DatoLH, DatoLW, DatoM;

  ROM #(.addrWidth(19), .dataWidth(16)) rom_1 (.addr(Dir[19:1]), .data(DatoM));
  Multiplexer #(.width(8)) multiplexer_1 (.in0(DatoM[7:0]), .in1(DatoM[15:8]), .out(DatoLH[7:0]), .sel(Dir[0]));
  Multiplexer multiplexer_2 (.in0(DatoLH[7]), .in1(1'b0), .out(DatoLH[15]), .sel(LHU));
  and and_1 (and_1_out, LW, Dir[0]);
  LED NoAlineado (.in(and_1_out));
  Multiplexer #(.width(16)) multiplexer_3 (.in0(DatoM), .in1({DatoM[7:0], DatoM[15:8]}), .out(DatoLW), .sel(BE));
  or or_1 (or_1_out, LH, LHU);
  Multiplexer #(.width(16)) multiplexer_4 (
    .in0(DatoLW), .in1({{8{DatoLH[15]}}, DatoLH[7:0]}), .out(Acumulador), .sel(or_1_out));

  // Other names for the same wires on the sheet: High[7:0] = DatoM[15:8]; Low[7:0] = DatoM[7:0];
  //   Half[7:0] = DatoLH[7:0]; Sig = DatoLH[7]; DatoLH[14:8] = {7{DatoLH[15]}}; Prop[7:0] = {8{DatoLH[15]}};
  //   A0 = Dir[0]; DirMem[18:0] = Dir[19:1]

  // Notes on the sheet:
  //   contents of rom_1 (hex, n*v repeats v):
  //   1234 5678 9abc deff 9f32
endmodule

module CPU32bits (
  input  BE,
  input  LW,
  input  LH,
  input  LHU,
  input  LB,
  input  LBU,
  input  [25:0] Dir,
  output [31:0] Acum
);

  wire and_1_out, and_2_out, and_3_out, or_1_out, or_2_out, or_3_out, or_4_out;
  wire [7:0] B0, B1, B2, B3, multiplexer_2_out;
  wire [15:0] multiplexer_1_out, multiplexer_4_out;
  wire [31:0] bit_extender_1_out, bit_extender_2_out, bit_extender_3_out, bit_extender_4_out, DatoB, DatoH,
       DatoW, multiplexer_6_out;

  ROM #(.addrWidth(24), .dataWidth(32)) rom_1 (.addr(Dir[25:2]), .data({B3, B2, B1, B0}));
  Multiplexer #(.select(2), .width(16)) multiplexer_1 (
    .in0({B1, B0}), .in1({B2, B1}), .in2({B3, B2}), .out(multiplexer_1_out), .sel(Dir[1:0]));  // open: in3
  Multiplexer #(.select(2), .width(8)) multiplexer_2 (
    .in0(B0), .in1(B1), .in2(B2), .in3(B3), .out(multiplexer_2_out), .sel(Dir[1:0]));
  Multiplexer #(.width(32)) multiplexer_3 (.in0({B3, B2, B1, B0}), .in1({B0, B1, B2, B3}), .out(DatoW), .sel(BE));
  assign bit_extender_1_out = {{24{multiplexer_2_out[7]}}, multiplexer_2_out};  // Bit_Extender bit_extender_1
  assign bit_extender_2_out = {{24{1'b0}}, multiplexer_2_out};  // Bit_Extender bit_extender_2
  or or_1 (or_1_out, Dir[0], Dir[1]);
  Multiplexer #(.width(16)) multiplexer_4 (
    .in0(multiplexer_1_out), .in1({multiplexer_1_out[7:0], multiplexer_1_out[15:8]}),
    .out(multiplexer_4_out), .sel(BE));
  Multiplexer #(.width(32)) multiplexer_5 (.in0(bit_extender_1_out), .in1(bit_extender_2_out), .out(DatoB), .sel(LBU));
  Multiplexer #(.width(32)) multiplexer_6 (.in0(DatoH), .in1(DatoB), .out(multiplexer_6_out), .sel(or_2_out));
  or or_2 (or_2_out, LBU, LB);
  and and_1 (and_1_out, or_1_out, LW);
  LED NoAlineado32 (.in(and_1_out));
  assign bit_extender_3_out = {{16{multiplexer_4_out[15]}}, multiplexer_4_out};  // Bit_Extender bit_extender_3
  Multiplexer #(.width(32)) multiplexer_7 (.in0(bit_extender_3_out), .in1(bit_extender_4_out), .out(DatoH), .sel(LHU));
  assign bit_extender_4_out = {{16{1'b0}}, multiplexer_4_out};  // Bit_Extender bit_extender_4
  Multiplexer #(.width(32)) multiplexer_8 (.in0(DatoW), .in1(multiplexer_6_out), .out(Acum), .sel(or_3_out));
  or or_3 (or_3_out, or_2_out, LH, LHU);
  and and_2 (and_2_out, Dir[0], Dir[1]);
  and and_3 (and_3_out, and_2_out, or_4_out);
  or or_4 (or_4_out, LH, LHU);
  LED NoAlineado16 (.in(and_3_out));

  // Other names for the same wires on the sheet: DatoM[31:0] = {B3, B2, B1, B0}; LWBE[31:0] = {B0, B1, B2, B3};
  //   A0 = Dir[0]; Sel[1:0] = Dir[1:0]; A1 = Dir[1]; DirMem[23:0] = Dir[25:2]

  // Notes on the sheet:
  //   contents of rom_1 (hex, n*v repeats v):
  //   1234567 89abcdef
endmodule
