// Logisim project FSM_Completo.circ as structural Verilog: 4 circuits, main circuit main
module DFF (
  input  NotCLR,
  input  D,
  input  Clock,
  output Q,
  output NotQ
);

  wire and_1_out, and_2_out, and_3_out, and_4_out, not_1_out, not_2_out, not_3_out, not_4_out;

  not not_1 (not_1_out, Clock);
  and and_1 (and_1_out, NotCLR, D);
  not not_2 (not_2_out, not_1_out);
  not not_3 (not_3_out, not_2_out);
  not not_4 (not_4_out, and_1_out);
  and and_2 (and_2_out, ~Clock, ~not_3_out);  // AND_Gate
  and and_3 (and_3_out, not_4_out, and_2_out);
  and and_4 (and_4_out, and_2_out, and_1_out);
  nor nor_1 (Q, and_3_out, NotQ);
  nor nor_2 (NotQ, Q, and_4_out);
endmodule

module main (
  input  Reset,
  output out_2,
  output out_3,
  output out_4,
  output out_5,
  output out_6,
  output out_7,
  output out_8,
  output out_9,
  output out_10,
  output out_11,
  output out_12
);

  wire and_1_out, and_2_out, and_3_out, and_4_out, and_5_out, and_6_out, and_7_out, and_8_out, and_9_out,
       and_10_out, and_11_out, and_12_out, and_13_out, and_14_out, and_15_out, and_16_out, and_17_out,
       Clock_out, multiplexer_1_out, multiplexer_2_out, not_1_out;

  Contador4bits contador4bits_1 (
    .T(1'b1), .Clk(Clock_out), .NotClr(and_5_out), .A(out_11), .B(out_10), .C(out_9), .D(out_8));
  or or_1 (out_6, and_1_out, and_2_out);
  and and_1 (and_1_out, out_8, out_9, ~out_10, out_11, ~out_2, ~out_3);  // AND_Gate
  and and_2 (and_2_out, ~out_8, ~out_9, out_10, ~out_11, out_2, out_3);  // AND_Gate
  DFF dff_1 (.Clock(Clock_out), .Q(out_2), .D(multiplexer_1_out), .NotCLR(Reset));  // open: NotQ
  Multiplexer #(.select(2), .enable("false")) multiplexer_1 (
    .in0(out_2), .in1(1'b1), .in2(1'b0), .out(multiplexer_1_out), .sel({out_6, out_7}));  // open: in3
  or or_2 (out_7, and_3_out, and_4_out);
  and and_3 (and_3_out, ~out_8, out_9, ~out_10, ~out_11, ~out_2, out_3);  // AND_Gate
  and and_4 (and_4_out, out_8, ~out_9, ~out_10, out_11, out_2, ~out_3);  // AND_Gate
  Clock Clock (.out(Clock_out));
  and and_5 (and_5_out, Reset, out_12);
  and and_6 (and_6_out, ~out_8, out_9, ~out_10, ~out_11, ~out_2, out_3);  // AND_Gate
  or or_3 (out_5, and_6_out, and_7_out);
  and and_7 (and_7_out, ~out_8, ~out_9, out_10, ~out_11, out_2, out_3);  // AND_Gate
  and and_8 (and_8_out, out_8, out_9, ~out_10, out_11, ~out_2, ~out_3);  // AND_Gate
  and and_9 (and_9_out, ~out_8, out_9, ~out_10, ~out_11, ~out_2, out_3);  // AND_Gate
  and and_10 (and_10_out, out_8, ~out_9, ~out_10, out_11, out_2, ~out_3);  // AND_Gate
  and and_11 (and_11_out, ~out_8, ~out_9, out_10, ~out_11, out_2, out_3);  // AND_Gate
  DFF dff_2 (.Clock(Clock_out), .Q(out_3), .D(multiplexer_2_out), .NotCLR(Reset));  // open: NotQ
  Multiplexer #(.select(2), .enable("false")) multiplexer_2 (
    .in0(out_3), .in1(1'b1), .in2(1'b0), .out(multiplexer_2_out), .sel({out_5, out_4}));  // open: in3
  or or_4 (out_4, and_12_out, and_13_out);
  and and_12 (and_12_out, out_8, out_9, ~out_10, out_11, ~out_2, ~out_3);  // AND_Gate
  and and_13 (and_13_out, out_8, ~out_9, ~out_10, out_11, out_2, ~out_3);  // AND_Gate
  nor nor_1 (out_12, and_8_out, and_9_out, and_10_out, and_11_out);
  LED led_1 (.in(out_2));
  and and_14 (and_14_out, ~out_2, out_3);  // AND_Gate
  LED led_2 (.in(and_14_out));
  and and_15 (and_15_out, ~out_2, ~out_3);  // AND_Gate
  LED led_3 (.in(and_15_out));
  LED led_4 (.in(not_1_out));
  not not_1 (not_1_out, out_2);
  and and_16 (and_16_out, out_2, ~out_3);  // AND_Gate
  LED led_5 (.in(and_17_out));
  and and_17 (and_17_out, out_3, out_2);
  LED led_6 (.in(and_16_out));
endmodule

module Contador4bits (
  input  T,
  input  Clk,
  input  NotClr,
  output A,
  output B,
  output C,
  output D
);

  wire and_1_out, and_2_out;

  TFF tff_1 (.NotCLR(NotClr), .T(T), .Clock(Clk), .Q(A));  // open: NotQ
  TFF tff_2 (.NotCLR(NotClr), .T(A), .Clock(Clk), .Q(B));  // open: NotQ
  TFF tff_3 (.NotCLR(NotClr), .T(and_1_out), .Clock(Clk), .Q(C));  // open: NotQ
  and and_1 (and_1_out, A, B);
  TFF tff_4 (.NotCLR(NotClr), .T(and_2_out), .Clock(Clk), .Q(D));  // open: NotQ
  and and_2 (and_2_out, and_1_out, C);
endmodule

module TFF (
  input  NotCLR,
  input  T,
  input  Clock,
  output Q,
  output NotQ
);

  wire and_1_out, and_2_out, and_3_out, and_4_out, not_1_out, not_2_out, not_3_out, not_4_out, xor_1_out;

  xor xor_1 (xor_1_out, Q, T);
  and and_1 (and_1_out, NotCLR, xor_1_out);
  not not_1 (not_1_out, not_2_out);
  not not_2 (not_2_out, Clock);
  and and_2 (and_2_out, ~Clock, ~not_3_out);  // AND_Gate
  not not_3 (not_3_out, not_1_out);
  not not_4 (not_4_out, and_1_out);
  and and_3 (and_3_out, not_4_out, and_2_out);
  and and_4 (and_4_out, and_2_out, and_1_out);
  nor nor_1 (Q, and_3_out, NotQ);
  nor nor_2 (NotQ, Q, and_4_out);
endmodule
