// Logisim project Untitled.circ as structural Verilog: 1 circuit, main circuit main
module main (
  input  in_1
);

  wire A, and_1_out, and_2_out, and_3_out, and_4_out, B, C, Clk, Clr, or_1_out, xor_1_out, xor_2_out;

  or or_1 (or_1_out, B, A);
  LED led_1 (.in(or_1_out));
  D_Flip_Flop d_ff_1 (.clk(Clk), .D(and_1_out), .Q(C));  // open: Qn, preset, en, reset
  and and_1 (and_1_out, ~C, ~Clr);  // AND_Gate
  xor xor_1 (xor_1_out, C, B);
  and and_2 (and_2_out, xor_1_out, ~Clr);  // AND_Gate
  and and_3 (and_3_out, B, C);
  xor xor_2 (xor_2_out, and_3_out, A);
  D_Flip_Flop d_ff_2 (.clk(Clk), .D(and_2_out), .Q(B));  // open: Qn, preset, en, reset
  D_Flip_Flop d_ff_3 (.clk(Clk), .D(and_4_out), .Q(A));  // open: Qn, preset, en, reset
  and and_4 (and_4_out, xor_2_out, ~Clr);  // AND_Gate
  and and_5 (Clr, ~C, ~B, A);  // AND_Gate
  Hex_Digit_Display hex_digit_display_1 (.value({in_1, A, B, C}));  // open: dp
  Clock clock_1 (.out(Clk));
endmodule
